// Logisim project addsub_machine.circ as structural Verilog: 10 circuits, main circuit MAIN
module Addsub (
  input  [3:0] \input ,
  input  load,
  input  reset,
  input  [1:0] sel_a,
  input  [1:0] sel_b,
  input  [1:0] sel_d,
  input  op,
  output [3:0] reg00,
  output [3:0] reg01,
  output [3:0] reg10,
  output [3:0] reg11
);

  Clock clk ();  // open: out
  MAIN addsub (
    .\input (\input ), .load(load), .sel_d(sel_d), .reset(reset), .op(op), .sel_a(sel_a), .sel_b(sel_b),
    .reg00(reg00), .reg01(reg01), .reg10(reg10), .reg11(reg11));  // open: sel_a_value, sel_b_value, result
endmodule

module MAIN (
  input  [3:0] \input ,
  input  load,
  input  [1:0] sel_d,
  input  reset,
  input  op,
  input  [1:0] sel_a,
  input  [1:0] sel_b,
  output [3:0] reg00,
  output [3:0] sel_a_value,
  output [3:0] reg01,
  output [3:0] reg10,
  output [3:0] sel_b_value,
  output [3:0] reg11,
  output [3:0] result
);

  wire clock_out, demultiplexer_2_out0, demultiplexer_2_out1, demultiplexer_2_out2, demultiplexer_2_out3,
       not_1_out, or_1_out;
  wire [3:0] demultiplexer_1_out0, demultiplexer_1_out1, demultiplexer_1_out2, demultiplexer_1_out3,
       \zweierkomplement_mit_switch_1_output__unverändert_oder_zweierkomplement ;

  Demultiplexer #(.select(2), .width(4)) demultiplexer_1 (
    .out0(demultiplexer_1_out0), .out1(demultiplexer_1_out1), .out2(demultiplexer_1_out2),
    .out3(demultiplexer_1_out3), .in(\input ), .sel(sel_d), .en(load));
  Demultiplexer #(.select(2)) demultiplexer_2 (
    .out0(demultiplexer_2_out0), .out1(demultiplexer_2_out1), .out2(demultiplexer_2_out2),
    .out3(demultiplexer_2_out3), .in(clock_out), .sel(sel_d), .en(or_1_out));
  Clock clock (.out(clock_out));
  or or_1 (or_1_out, load, not_1_out);
  _4_bit_D_FF u_4_bit_d_ff_1 (
    .enable(not_1_out), .load(load), .clock(demultiplexer_2_out0), .\input (demultiplexer_1_out0),
    .reset(reset), .output00(reg00));
  _4_bit_D_FF u_4_bit_d_ff_2 (
    .enable(not_1_out), .load(load), .clock(demultiplexer_2_out1), .\input (demultiplexer_1_out1),
    .reset(reset), .output00(reg01));
  _4_bit_D_FF u_4_bit_d_ff_3 (
    .enable(not_1_out), .load(load), .clock(demultiplexer_2_out2), .\input (demultiplexer_1_out2),
    .reset(reset), .output00(reg10));
  _4_bit_D_FF u_4_bit_d_ff_4 (
    .enable(not_1_out), .load(load), .clock(demultiplexer_2_out3), .\input (demultiplexer_1_out3),
    .reset(reset), .output00(reg11));
  Demultiplexer #(.select(2), .width(4)) demultiplexer_3 (
    .out0(demultiplexer_1_out0), .out1(demultiplexer_1_out1), .out2(demultiplexer_1_out2),
    .out3(demultiplexer_1_out3), .in(result), .sel(sel_d), .en(not_1_out));
  not not_1 (not_1_out, load);
  Multiplexer #(.select(2), .width(4)) multiplexer_1 (
    .in0(reg00), .in1(reg01), .in2(reg10), .in3(reg11), .out(sel_a_value), .sel(sel_a), .en(not_1_out));
  Multiplexer #(.select(2), .width(4)) multiplexer_2 (
    .in0(reg00), .in1(reg01), .in2(reg10), .in3(reg11), .out(sel_b_value), .sel(sel_b), .en(not_1_out));
  _4_Bit_Addierer u_4_bit_addierer_1 (
    .Input_Num1(sel_a_value),
    .Input_Num2(\zweierkomplement_mit_switch_1_output__unverändert_oder_zweierkomplement ), .SumOutput(result));
  Zweierkomplement_mit_Switch zweierkomplement_mit_switch_1 (
    .Input(sel_b_value), .OP_ifsub_1__ifadd_0(op),
    .\Output__unverändert_oder_Zweierkomplement (\zweierkomplement_mit_switch_1_output__unverändert_oder_zweierkomplement ));
endmodule

module _4_bit_D_FF (
  input  enable,
  input  load,
  input  clock,
  input  [3:0] \input ,
  input  reset,
  output [3:0] output00
);

  wire or_1_out;

  or or_1 (or_1_out, enable, load);
  D_Flip_Flop d_ff_1 (.clk(clock), .D(\input [0]), .Q(output00[0]), .en(or_1_out), .reset(reset));  // open: Qn, preset
  D_Flip_Flop d_ff_2 (.clk(clock), .D(\input [1]), .Q(output00[1]), .en(or_1_out), .reset(reset));  // open: Qn, preset
  D_Flip_Flop d_ff_3 (.clk(clock), .D(\input [2]), .Q(output00[2]), .en(or_1_out), .reset(reset));  // open: Qn, preset
  D_Flip_Flop d_ff_4 (.clk(clock), .D(\input [3]), .Q(output00[3]), .en(or_1_out), .reset(reset));  // open: Qn, preset
endmodule

module _4_Bit_Addierer (
  input  [3:0] Input_Num1,
  input  [3:0] Input_Num2,
  output [3:0] SumOutput
);

  wire halbaddierer_1_overflow, volladdierer_1_overflow_out, volladdierer_2_overflow_out,
       volladdierer_3_overflow_out;

  Halbaddierer halbaddierer_1 (
    .in_1(Input_Num2[0]), .in_2(Input_Num1[0]), .Overflow(halbaddierer_1_overflow), .Sum(SumOutput[0]));
  Volladdierer volladdierer_1 (
    .Num1(Input_Num1[1]), .Num2(Input_Num2[1]), .Overflow_in(halbaddierer_1_overflow),
    .Sum_Output(SumOutput[1]), .Overflow_Out(volladdierer_1_overflow_out));
  Volladdierer volladdierer_2 (
    .Num1(Input_Num1[2]), .Num2(Input_Num2[2]), .Overflow_in(volladdierer_1_overflow_out),
    .Sum_Output(SumOutput[2]), .Overflow_Out(volladdierer_2_overflow_out));
  Volladdierer volladdierer_3 (
    .Num1(Input_Num1[3]), .Num2(Input_Num2[3]), .Overflow_in(volladdierer_2_overflow_out),
    .Sum_Output(SumOutput[3]), .Overflow_Out(volladdierer_3_overflow_out));
  LED LED (.in(volladdierer_3_overflow_out));
endmodule

module Zweierkomplement_mit_Switch (
  input  [3:0] Input,
  input  OP_ifsub_1__ifadd_0,
  output [3:0] \Output__unverändert_oder_Zweierkomplement 
);

  wire halbaddierer_2_overflow, halbaddierer_3_overflow, halbaddierer_4_overflow, xor_1_out, xor_2_out,
       xor_3_out, xor_4_out;

  xor xor_1 (xor_1_out, Input[3], OP_ifsub_1__ifadd_0);
  xor xor_2 (xor_2_out, Input[2], OP_ifsub_1__ifadd_0);
  Halbaddierer halbaddierer_1 (
    .in_1(xor_1_out), .in_2(halbaddierer_2_overflow), .Sum(\Output__unverändert_oder_Zweierkomplement [3]));  // open: Overflow
  Halbaddierer halbaddierer_2 (
    .in_1(xor_2_out), .in_2(halbaddierer_3_overflow), .Overflow(halbaddierer_2_overflow),
    .Sum(\Output__unverändert_oder_Zweierkomplement [2]));
  xor xor_3 (xor_3_out, Input[1], OP_ifsub_1__ifadd_0);
  Halbaddierer halbaddierer_3 (
    .in_1(xor_3_out), .in_2(halbaddierer_4_overflow), .Overflow(halbaddierer_3_overflow),
    .Sum(\Output__unverändert_oder_Zweierkomplement [1]));
  xor xor_4 (xor_4_out, Input[0], OP_ifsub_1__ifadd_0);
  Halbaddierer halbaddierer_4 (
    .in_1(xor_4_out), .in_2(OP_ifsub_1__ifadd_0), .Overflow(halbaddierer_4_overflow),
    .Sum(\Output__unverändert_oder_Zweierkomplement [0]));
endmodule

module Volladdierer (
  input  Num1,
  input  Num2,
  input  Overflow_in,
  output Sum_Output,
  output Overflow_Out
);

  wire and_1_out, and_2_out, xor_1_out;

  xor xor_1 (xor_1_out, Num1, Num2);
  and and_1 (and_1_out, xor_1_out, Overflow_in);
  and and_2 (and_2_out, Num1, Num2);
  xor xor_2 (Sum_Output, xor_1_out, Overflow_in);
  or or_1 (Overflow_Out, and_1_out, and_2_out);
endmodule

module Halbaddierer (
  input  in_1,
  input  in_2,
  output Overflow,
  output Sum
);

  and and_1 (Overflow, in_1, in_2);
  xor xor_1 (Sum, in_1, in_2);
endmodule

module _4_bit_SR_FF__not_in_use (
  input  enable,
  input  load,
  input  clock,
  input  [3:0] \input ,
  input  reset,
  input  R,
  output [3:0] output00
);

  wire or_1_out;

  or or_1 (or_1_out, enable, load);
  S_R_Flip_Flop s_r_ff_1 (
    .S(\input [0]), .clk(clock), .R(R), .Q(output00[0]), .reset(reset), .en(or_1_out));  // open: Qn, preset
  S_R_Flip_Flop s_r_ff_2 (
    .S(\input [1]), .clk(clock), .R(R), .Q(output00[1]), .reset(reset), .en(or_1_out));  // open: Qn, preset
  S_R_Flip_Flop s_r_ff_3 (
    .S(\input [2]), .clk(clock), .R(R), .Q(output00[2]), .reset(reset), .en(or_1_out));  // open: Qn, preset
  S_R_Flip_Flop s_r_ff_4 (
    .S(\input [3]), .clk(clock), .R(R), .Q(output00[3]), .reset(reset), .en(or_1_out));  // open: Qn, preset
endmodule

module _4_bit_flip_flop__not_in_use (
  input  load_trigger,
  input  reset_trigger,
  input  Clk_input,
  input  [3:0] Input_Num,
  output [3:0] Output_num
);

  wire and_1_out;

  D_Flip_Flop d_ff_1 (
    .clk(Clk_input), .D(Input_Num[0]), .Q(Output_num[0]), .en(load_trigger), .reset(and_1_out));  // open: Qn, preset
  D_Flip_Flop d_ff_2 (
    .clk(Clk_input), .D(Input_Num[1]), .Q(Output_num[1]), .en(load_trigger), .reset(and_1_out));  // open: Qn, preset
  D_Flip_Flop d_ff_3 (
    .clk(Clk_input), .D(Input_Num[2]), .Q(Output_num[2]), .en(load_trigger), .reset(and_1_out));  // open: Qn, preset
  D_Flip_Flop d_ff_4 (
    .clk(Clk_input), .D(Input_Num[3]), .Q(Output_num[3]), .en(load_trigger), .reset(and_1_out));  // open: Qn, preset
  and and_1 (and_1_out, Clk_input, reset_trigger);
endmodule

module Main__not_in_use (
  input  [3:0] \input ,
  input  load,
  input  [1:0] sel_d,
  input  reset,
  input  R,
  input  op,
  input  [1:0] sel_a,
  input  [1:0] sel_b,
  output [3:0] reg00,
  output [3:0] out_10,
  output [3:0] reg01,
  output [3:0] reg10,
  output [3:0] out_13,
  output [3:0] reg11,
  output [3:0] Result
);

  wire clock_out, not_1_out;
  wire [3:0] demultiplexer_1_out0, demultiplexer_1_out1, demultiplexer_1_out2, demultiplexer_1_out3,
       \zweierkomplement_mit_switch_1_output__unverändert_oder_zweierkomplement ;

  Demultiplexer #(.select(2), .width(4)) demultiplexer_1 (
    .out0(demultiplexer_1_out0), .out1(demultiplexer_1_out1), .out2(demultiplexer_1_out2),
    .out3(demultiplexer_1_out3), .in(\input ), .sel(sel_d), .en(load));
  Clock clock (.out(clock_out));
  _4_bit_SR_FF__not_in_use u_4_bit_sr_ff_not_in_use_1 (
    .enable(not_1_out), .load(load), .clock(clock_out), .\input (demultiplexer_1_out0), .reset(reset), .R(R),
    .output00(reg00));
  _4_bit_SR_FF__not_in_use u_4_bit_sr_ff_not_in_use_2 (
    .enable(not_1_out), .load(load), .clock(clock_out), .\input (demultiplexer_1_out1), .reset(reset), .R(R),
    .output00(reg01));
  _4_bit_SR_FF__not_in_use u_4_bit_sr_ff_not_in_use_3 (
    .enable(not_1_out), .load(load), .clock(clock_out), .\input (demultiplexer_1_out2), .reset(reset), .R(R),
    .output00(reg10));
  _4_bit_SR_FF__not_in_use u_4_bit_sr_ff_not_in_use_4 (
    .enable(not_1_out), .load(load), .clock(clock_out), .\input (demultiplexer_1_out3), .reset(reset), .R(R),
    .output00(reg11));
  Demultiplexer #(.select(2), .width(4)) demultiplexer_2 (
    .out0(demultiplexer_1_out0), .out1(demultiplexer_1_out1), .out2(demultiplexer_1_out2),
    .out3(demultiplexer_1_out3), .in(Result), .sel(sel_a), .en(not_1_out));
  not not_1 (not_1_out, load);
  Multiplexer #(.select(2), .width(4)) multiplexer_1 (
    .in0(reg00), .in1(reg01), .in2(reg10), .in3(reg11), .out(out_10), .sel(sel_a), .en(not_1_out));
  Multiplexer #(.select(2), .width(4)) multiplexer_2 (
    .in0(reg00), .in1(reg01), .in2(reg10), .in3(reg11), .out(out_13), .sel(sel_b), .en(not_1_out));
  _4_Bit_Addierer u_4_bit_addierer_1 (
    .Input_Num1(\zweierkomplement_mit_switch_1_output__unverändert_oder_zweierkomplement ),
    .Input_Num2(out_13), .SumOutput(Result));
  Zweierkomplement_mit_Switch zweierkomplement_mit_switch_1 (
    .Input(out_10), .OP_ifsub_1__ifadd_0(op),
    .\Output__unverändert_oder_Zweierkomplement (\zweierkomplement_mit_switch_1_output__unverändert_oder_zweierkomplement ));
endmodule
